# Fritzing sketch SimonSays (saved by Fritzing 0.9.2b)
breadboards: 1

parts:
  Part1 = Arduino Uno (Rev3) - ICSP
  U1 = LCD-16X2 [package=lcd-16x2_noholes]
  LED1 = LED - 5mm [color="Red (633nm)" package="5 mm [THT]"]
  LED2 = LED - 5mm [color="Green (555nm)" package="5 mm [THT]"]
  LED3 = LED - 5mm [color="White (6500K)" package="5 mm [THT]"]
  LED4 = LED - 5mm [color="Yellow (595nm)" package="5 mm [THT]"]
  J1 = Piezo Speaker
  Part2 = SRF05 Ultrasonic Rangefinder
  R2 = Resistor [tolerance=±5% resistance=220 package="2512 [SMD]"]
  R3 = Resistor [tolerance=±5% resistance=220 package="2512 [SMD]"]
  R4 = Resistor [tolerance=±5% resistance=220 package="2512 [SMD]"]
  R5 = Resistor [tolerance=±5% resistance=220 package="2512 [SMD]"]
  R6 = Resistor [tolerance=±5% resistance=220 package="2512 [SMD]"]
  R7 = Rotary Potentiometer (Small) [maximum_resistance=100kΩ package=THT]
  Part3 = Thumb Joystick

nets:
  N1: Part1.A0, Part3.HORZ
  N2: Part1.A1, Part3.VERT
  N3: Part1.A2, Part2.Echo
  N4: Part1.D8, R2.Pin_1
  N5: Part1.D9_PWM, R3.Pin_1
  N6: Part1.D10_PWM/SS, J1.pin2
  N7: Part1.D11_PWM/MOSI, U1.E
  N8: Part1.D12/MISO, U1.RS
  N9: Part1.D13/SCK, Part2.Trig
  N10: Part1.D2, U1.DB7
  N11: Part1.D3_PWM, U1.DB6
  N12: Part1.D4, U1.DB5
  N13: Part1.D5_PWM, U1.DB4
  N14: Part1.D6_PWM, R4.Pin_1
  N15: Part1.D7, R5.Pin_1
  VCC: Part1.5V, U1.VDD, Part2.VCC, R6.Pin_0, R7.leg1, Part3.VCC
  GND: Part1.GND, U1.VSS, U1.R_W, U1.K, LED1.cathode, LED2.cathode, LED3.cathode, J1.pin1, Part2.GND, R7.leg2, Part3.GND, Part3.SEL
  N16: U1.VO, R7.wiper
  N17: U1.A, R6.Pin_1
  N18: LED1.anode, R4.Pin_0
  N19: LED2.anode, R5.Pin_0
  N20: LED3.anode, R2.Pin_0
  N21: LED4.anode, R3.Pin_0
